# Fritzing sketch wifiCamera (saved by Fritzing 0.8.7b)

parts:
  Componente1 = Arduino Uno (Rev3)  # not connected
  Componente2 = Arduino Prototyping Shield
  CC3K1 = Adafruit CC3000 WiFi Breakout
  CAMERA1 = TTL Serial JPEG Camera
  R1 = Resistor [tolerance=±5% resistance=10k package=THT]
  R2 = Resistor [tolerance=±5% resistance=10k package=THT]

nets:
  +5V: Componente2.+5V, Componente2.N$77, CC3K1.VIN, CAMERA1.5V
  GND: Componente2.GND, Componente2.N$118, Componente2.N$393, CC3K1.GND, CAMERA1.GND, R2.Pin_1
  N1: Componente2.D10, Componente2.N$48, CC3K1.CS
  N2: Componente2.D11, Componente2.N$62, CC3K1.MOSI
  N3: Componente2.D12, Componente2.N$72, CC3K1.MISO
  N4: Componente2.D13, Componente2.N$86, CC3K1.CLK
  N5: Componente2.D2, R1.Pin_0
  N6: Componente2.D3, Componente2.N$27, CC3K1.IRQ
  N7: Componente2.D4, CAMERA1.TX
  N8: Componente2.D5, Componente2.N$37, CC3K1.VBEN
  N9: Componente2.N$76, CC3K1.3V3
  N10: Componente2.N$405, CAMERA1.RX, R2.Pin_0
  N11: Componente2.N$406, R1.Pin_1

custom parts:
  Adafruit CC3000 WiFi Breakout: CC3000 WiFi Breakout
  TTL Serial JPEG Camera: TTL Serial JPEG Camera with NTSC Out
